# Fritzing sketch dht11_esp8266 (saved by Fritzing 0.9.3b)
breadboards: 1

parts:
  Adafruit_HUZZAH_ESP8266_Breakout1 = Adafruit HUZZAH ESP8266 Breakout [part_number=2471]
  M1 = Humidity and Temperature Sensor DHT11

nets:
  GND: Adafruit_HUZZAH_ESP8266_Breakout1.GND, M1.GND
  N1: Adafruit_HUZZAH_ESP8266_Breakout1.V+, M1.Vcc
  N2: Adafruit_HUZZAH_ESP8266_Breakout1.#4, M1.Data

custom parts:
  Humidity and Temperature Sensor DHT11: Digital relative humidity & temperature sensor DHT11
