# Fritzing sketch hcsr04_esp8266 (saved by Fritzing 0.9.3b)
breadboards: 1

parts:
  Adafruit_HUZZAH_ESP8266_Breakout1 = Adafruit HUZZAH ESP8266 Breakout [part_number=2471]
  HC-SR04_Sensor_1 = HC-SR04 Ultrasonic Distance Sensor

nets:
  GND: Adafruit_HUZZAH_ESP8266_Breakout1.GND, HC-SR04_Sensor_1.GND
  N1: Adafruit_HUZZAH_ESP8266_Breakout1.V+, HC-SR04_Sensor_1.VCC
  N2: Adafruit_HUZZAH_ESP8266_Breakout1.#12, HC-SR04_Sensor_1.ECHO
  N3: Adafruit_HUZZAH_ESP8266_Breakout1.#14, HC-SR04_Sensor_1.TRIG
